# Fritzing sketch circuito (saved by Fritzing 0.9.3b)
breadboards: 1

parts:
  Raspberry_Pi_1 = Raspberry Pi 3 [part_number=RPI-3-V1.2]
  M1 = fc-51 [package=THT]
  M2 = fc-51 [package=THT]
  M3 = DC Motor  # not connected
  M4 = DC Motor  # not connected
  IC1 = L293D [package=THT]

nets:
  N1: Raspberry_Pi_1.GPIO14, Raspberry_Pi_1.GND, M1.pin2, M2.pin2, IC1.+V
  N2: Raspberry_Pi_1.5V, M1.pin3, M2.pin3, IC1.Enable_1, IC1.0V
